# Fritzing sketch Arduino-Hall-LCD (saved by Fritzing 0.9.3b)
breadboards: 1

parts:
  Součástka1 = Arduino Uno (Rev3)
  LCD2 = LCD screen
  LCM1602_IIC2 = LCM1602 IIC [part_number="LCM1602 IIC" chip_label="LCM1602 IIC" package="DIP (Dual Inline) [THT]"]
  U1 = mystery part, 3 pins [chip_label=TLE4905L]
  R1 = Resistor [tolerance=±1% resistance=4.7k package=THT]

nets:
  N1: Součástka1.A4/SDA, LCM1602_IIC2.SDA
  N2: Součástka1.A5/SCL, LCM1602_IIC2.SCL
  N3: Součástka1.D2, U1.pin3, R1.Pin_1
  5V: Součástka1.5V, LCM1602_IIC2.VCC, U1.pin1, R1.Pin_0
  GND: Součástka1.GND, LCM1602_IIC2.GND, U1.pin2
  VSS: LCD2.VSS, LCM1602_IIC2.VSS
  VDD: LCD2.VDD, LCM1602_IIC2.VDD
  N4: LCD2.V0, LCM1602_IIC2.V0
  N5: LCD2.RS, LCM1602_IIC2.RS
  N6: LCD2.R/W, LCM1602_IIC2.RW
  N7: LCD2.E, LCM1602_IIC2.E
  N8: LCD2.DB0, LCM1602_IIC2.D0
  N9: LCD2.DB1, LCM1602_IIC2.D1
  N10: LCD2.DB2, LCM1602_IIC2.D2
  N11: LCD2.DB3, LCM1602_IIC2.D3
  N12: LCD2.DB4, LCM1602_IIC2.D4
  N13: LCD2.DB5, LCM1602_IIC2.D5
  N14: LCD2.DB6, LCM1602_IIC2.D6
  N15: LCD2.DB7, LCM1602_IIC2.D7
  N16: LCD2.LED+, LCM1602_IIC2.A
  N17: LCD2.LED-, LCM1602_IIC2.K

custom parts:
  LCM1602 IIC: I2C-Module to use a 1602 or 2004 LCD on with the wire.h libory Serial LCD Modul
